# Fritzing sketch chibit (saved by Fritzing 0.9.2b)
breadboards: 1

parts:
  ESP2 = ESP 12E
  Part4 = LilyPad Button Board
  R10 = Resistor [tolerance=±5% resistance=1k package=THT]
  R9 = Textile Stretch Sensor [part_number=PW052]
  Part3 = LilyPad Coin Cell Battery Holder

nets:
  N1: ESP2.GND, Part4.-, R10.Pin_0
  N2: ESP2.VCC, ESP2.GPIO13, R9.pin_1
  N3: ESP2.ADC, R10.Pin_1, R9.pin_0
  N4: Part4.S, Part3.+

custom parts:
  ESP 12E: ESP 12e module with spi interface and wifi connection
